// Logisim project 2_arithmetic.circ as structural Verilog: 1 circuit, main circuit main
module main (
  input  [1:0] S1S0,
  input  ENABLE,
  input  Cin,
  input  A3,
  input  A2,
  input  A1,
  input  A0,
  input  B3,
  input  B2,
  input  B1,
  input  B0,
  input  in_12,
  output D3,
  output D2,
  output D1,
  output D0,
  output Cout
);

  wire adder_1_cout, adder_2_cout, adder_3_cout, multiplexer_1_out, multiplexer_2_out, multiplexer_3_out,
       multiplexer_4_out, not_1_out, not_2_out, not_3_out, not_4_out, not_5_out;

  not not_1 (not_1_out, in_12);
  not not_2 (not_2_out, B0);
  Multiplexer #(.select(2)) multiplexer_1 (
    .in0(B0), .in1(not_2_out), .in2(in_12), .in3(not_1_out), .out(multiplexer_1_out), .sel(S1S0), .en(ENABLE));
  not not_3 (not_3_out, B1);
  Multiplexer #(.select(2)) multiplexer_2 (
    .in0(B1), .in1(not_3_out), .in2(in_12), .in3(not_1_out), .out(multiplexer_2_out), .sel(S1S0), .en(ENABLE));
  not not_4 (not_4_out, B2);
  Multiplexer #(.select(2)) multiplexer_3 (
    .in0(B2), .in1(not_4_out), .in2(in_12), .in3(not_1_out), .out(multiplexer_3_out), .sel(S1S0), .en(ENABLE));
  not not_5 (not_5_out, B3);
  Multiplexer #(.select(2)) multiplexer_4 (
    .in0(B3), .in1(not_5_out), .in2(in_12), .in3(not_1_out), .out(multiplexer_4_out), .sel(S1S0), .en(ENABLE));
  Adder #(.width(1)) adder_1 (.a(A0), .b(multiplexer_1_out), .out(D0), .cin(Cin), .cout(adder_1_cout));
  Adder #(.width(1)) adder_2 (.a(A1), .b(multiplexer_2_out), .out(D1), .cin(adder_1_cout), .cout(adder_2_cout));
  Adder #(.width(1)) adder_3 (.a(A2), .b(multiplexer_3_out), .out(D2), .cin(adder_2_cout), .cout(adder_3_cout));
  Adder #(.width(1)) adder_4 (.a(A3), .b(multiplexer_4_out), .out(D3), .cin(adder_3_cout), .cout(Cout));

  // Notes on the sheet:
  //   Prac 2 : Arithmetic  Circuit
  //   Here Subtraction Operation 7 - 2 = 5 is performed..
  //   Prajapati Krish S
  //   230280107116
  //   Div : B /B1
  //   COA
endmodule
