// Logisim project DIVISON ALGO.circ as structural Verilog: 1 circuit, main circuit main
module main (
  input  [4:0] in_1,
  input  in_2,
  input  in_3,
  input  in_4,
  input  [3:0] in_5,
  input  [3:0] in_6,
  input  in_7,
  input  in_8,
  input  [2:0] in_9,
  output [8:0] out_10,
  output out_11,
  output [4:0] out_12
);

  wire clock_1_out;
  wire [3:0] bit_extender_3_out, Q_q, shifter_2_out;
  wire [4:0] A_q, adder_2_out, B_q, controlled_buffer_1_out, multiplexer_1_out, not_1_out, shifter_2_out_2;
  wire [8:0] bit_extender_1_out, bit_extender_2_out, not_2_out, shifter_1_out;

  Register #(.width(4)) Q (.D(bit_extender_3_out), .en(in_3), .Q(Q_q), .clk(clock_1_out));  // open: clr
  Register #(.width(5)) A (.D(multiplexer_1_out), .en(in_4), .Q(A_q), .clk(clock_1_out));  // open: clr
  Counter #(.width(3), .max('h7)) counter_1 (.load(in_8), .D(in_9), .clk(clock_1_out));  // open: count, Q, carry, clr
  Clock clock_1 (.out(clock_1_out));
  Register #(.width(5)) B (.D(in_1), .en(in_2), .Q(B_q), .clk(clock_1_out));  // open: clr
  assign bit_extender_1_out = {{4{1'b0}}, A_q};  // Bit_Extender bit_extender_1
  assign not_1_out = ~B_q;  // NOT_Gate not_1, 5 bits wide
  assign bit_extender_2_out = {{5{1'b0}}, Q_q};  // Bit_Extender bit_extender_2
  Shifter #(.width(9)) shifter_1 (.in(bit_extender_1_out), .\dist (in_5), .out(shifter_1_out));
  Adder #(.width(5)) adder_1 (
    .a(shifter_2_out_2), .b(not_1_out), .out({out_11, out_12[3:0]}), .cin(in_7));  // open: cout
  assign out_10 = bit_extender_2_out | shifter_1_out;  // OR_Gate or_1, 9 bits wide
  Multiplexer #(.width(5), .enable("false")) multiplexer_1 (
    .in0({out_11, out_12[3:0]}), .in1(adder_2_out), .out(multiplexer_1_out), .sel(out_11));
  assign controlled_buffer_1_out = out_11 ? {out_11, out_12[3:0]} : 5'bz;  // Controlled_Buffer controlled_buffer_1
  Shifter #(.width(9)) shifter_2 (.in(out_10), .\dist (in_6), .out({shifter_2_out_2, shifter_2_out}));
  Adder #(.width(5)) adder_2 (.a(controlled_buffer_1_out), .b(B_q), .out(adder_2_out));  // open: cin, cout
  not not_2 (not_2_out[0], out_11);
  Bit_Extender #(.in_width(9), .out_width(4)) bit_extender_3 (
    .in({not_2_out[8:4], shifter_2_out[3:1], not_2_out[0]}), .out(bit_extender_3_out));

  assign out_12[4] = out_11;

  // Notes on the sheet:
  //   Remainder
  //   Divisor
  //   Divident
  //   Quotient
  //   Practical 11 : Division Algorithm
  //   Prajapati Krish S
  //   230280107116
  //   B /B1
endmodule
