// Logisim project booth temp.circ as structural Verilog: 1 circuit, main circuit main
module main (
  input  [3:0] _2_s_com_0f_5,
  input  in_2,
  input  [3:0] in_3,
  input  in_4,
  input  in_5,
  input  [3:0] in_6,
  input  in_7,
  input  [3:0] in_8,
  input  in_9,
  input  in_10,
  input  [2:0] in_11,
  input  [2:0] in_12,
  output [1:0] out_13,
  output [8:0] AQQn_1,
  output [8:0] out_15,
  output [3:0] Q,
  output Qn_1,
  output [3:0] A
);

  wire clock_1_out, clock_2_out, comparator_1_eq, controlled_buffer_3_out, not_1_out, Qn_1_q;
  wire [2:0] counter_1_q;
  wire [3:0] A_q, adder_1_out, B_q, controlled_buffer_1_out, controlled_buffer_2_out, multiplexer_1_out, Q_q,
       subtractor_1_out;
  wire [8:0] bit_extender_1_out, bit_extender_2_out, bit_extender_3_out, shifter_1_out, shifter_2_out;

  Clock clock_1 (.out(clock_1_out));
  Register #(.width(4)) u_A (.D(controlled_buffer_2_out), .en(in_4), .Q(A_q), .clk(clock_1_out));  // open: clr
  Register #(.width(4)) u_Q (.D(controlled_buffer_1_out), .en(in_5), .Q(Q_q), .clk(clock_1_out));  // open: clr
  Register #(.width(4)) B (.D(_2_s_com_0f_5), .en(in_2), .Q(B_q), .clk(clock_1_out));  // open: clr
  Register #(.width(1)) u_Qn_1 (.D(controlled_buffer_3_out), .en(in_9), .Q(Qn_1_q), .clk(clock_1_out));  // open: clr
  Clock clock_2 (.out(clock_2_out));
  assign bit_extender_1_out = {{5{1'b0}}, Q_q};  // Bit_Extender bit_extender_1
  assign bit_extender_2_out = {{8{1'b0}}, Qn_1_q};  // Bit_Extender bit_extender_2
  Counter #(.width(3), .max('h7)) counter_1 (
    .load(in_10), .D(in_11), .Q(counter_1_q), .clk(clock_2_out));  // open: count, carry, clr
  Adder #(.width(4)) adder_1 (.a(B_q), .b(A_q), .out(adder_1_out));  // open: cin, cout
  Subtractor #(.width(4)) subtractor_1 (.a(A_q), .b(B_q), .out(subtractor_1_out));  // open: bin, bout
  Shifter #(.width(9)) shifter_1 (.in(bit_extender_1_out), .\dist (in_6), .out(shifter_1_out));
  Comparator #(.width(3)) comparator_1 (.a(counter_1_q), .b(in_12), .eq(comparator_1_eq));  // open: gt, lt
  assign controlled_buffer_1_out = not_1_out ? out_15[4:1] : 4'bz;  // Controlled_Buffer controlled_buffer_1
  assign controlled_buffer_2_out = not_1_out ? A : 4'bz;  // Controlled_Buffer controlled_buffer_2
  not not_1 (not_1_out, comparator_1_eq);
  Multiplexer #(.select(2), .width(4), .enable("false")) multiplexer_1 (
    .in0(A_q), .in1(adder_1_out), .in2(subtractor_1_out), .in3(A_q), .out(multiplexer_1_out),
    .sel(AQQn_1[1:0]));
  assign bit_extender_3_out = {{5{1'b0}}, multiplexer_1_out};  // Bit_Extender bit_extender_3
  assign controlled_buffer_3_out = not_1_out ? out_15[0] : 1'bz;  // Controlled_Buffer controlled_buffer_3
  Shifter #(.width(9)) shifter_2 (.in(bit_extender_3_out), .\dist (in_3), .out(shifter_2_out));
  assign AQQn_1 = shifter_2_out | shifter_1_out | bit_extender_2_out;  // OR_Gate or_1, 9 bits wide
  Shifter #(.width(9), .shift("ar")) shifter_3 (.in(AQQn_1), .\dist (in_8), .out({A, out_15[4:0]}));
  Register #(.width(9)) Ans (.D({A, out_15[4:0]}), .clk(clock_2_out));  // open: en, Q, clr

  assign out_13 = AQQn_1[1:0];
  assign out_15[8:5] = A;
  assign Q = out_15[4:1];
  assign Qn_1 = out_15[0];

  // Notes on the sheet:
  //   Booth Multiplication
  //   B = - 5 = 10 in 2's comp form ;  Q = 4.
  //   A+B
  //   A-B
  //   at sc = 1 , the answer is 014 in hexa which is -20  in decimal. It means after 4 counts we get answer.
  //   0000 q3q2q1q0 Qn+1
  //   At first Qn+1 = 0 , and sc  =  5  we have connected 0 to Qn+1 , but after first pass, we connect as per diagram..
  //   Prajapati Krish S
  //   230280107116
  //   B / B1
  //   Q
  //   A
  //   Qn+1
  //   A3A2A1A0 0000 Qn+1
  //   ans : 20
  //   in hexa 
endmodule
