// Logisim project myultiplication Rotation prac 8.circ as structural Verilog: 1 circuit, main circuit main
module main (
  input  [3:0] in_1,
  input  in_2,
  input  [3:0] in_3,
  input  [3:0] in_4,
  input  in_5,
  input  [2:0] in_6,
  input  in_7,
  input  [2:0] in_8,
  input  [3:0] in_9,
  output out_10,
  output [8:0] out_11,
  output [8:0] out_12,
  output [8:0] out_13,
  output [8:0] out_14,
  output [8:0] out_15,
  output [8:0] EAQ,
  output out_17,
  output [8:0] out_18,
  output [3:0] Q,
  output [3:0] A
);

  wire adder_1_cout, clock_1_out, clock_2_out, not_1_out;
  wire [2:0] counter_1_q;
  wire [3:0] A_q, adder_1_out, B_q, controlled_buffer_1_out, controlled_buffer_2_out, multiplexer_1_out;
  wire [3:1] Q_q;

  Clock clock_1 (.out(clock_1_out));
  Clock clock_2 (.out(clock_2_out));
  Register #(.width(4)) u_Q (.D(controlled_buffer_2_out), .Q({Q_q, out_10}), .clk(clock_1_out));  // open: en, clr
  Counter #(.width(3), .max('h4)) counter_1 (
    .load(in_5), .D(in_6), .count(in_7), .Q(counter_1_q), .clk(clock_2_out));  // open: carry, clr
  Register #(.width(4)) u_A (.D(controlled_buffer_1_out), .Q(A_q), .clk(clock_1_out));  // open: en, clr
  assign controlled_buffer_1_out = not_1_out ? A : 4'bz;  // Controlled_Buffer controlled_buffer_1
  assign out_13 = {{5{1'b0}}, {Q_q, out_10}};  // Bit_Extender bit_extender_1
  Comparator #(.width(3)) comparator_1 (.a(counter_1_q), .b(in_8), .eq(out_17));  // open: gt, lt
  not not_1 (not_1_out, out_17);
  assign controlled_buffer_2_out = not_1_out ? out_18[3:0] : 4'bz;  // Controlled_Buffer controlled_buffer_2
  Register #(.width(4)) B (.D(in_1), .Q(B_q), .clk(in_2));  // open: en, clr
  Adder #(.width(4)) adder_1 (.a(A_q), .b(B_q), .out(adder_1_out), .cout(adder_1_cout));  // open: cin
  assign out_12 = {{8{1'b0}}, adder_1_cout};  // Bit_Extender bit_extender_2
  Shifter #(.width(9), .shift("rr")) shifter_1 (.in(out_12), .\dist (in_4), .out(out_15));
  Multiplexer #(.width(4), .enable("false")) multiplexer_1 (
    .in0(A_q), .in1(adder_1_out), .out(multiplexer_1_out), .sel(out_10));
  assign EAQ = out_15 | out_14 | out_13;  // OR_Gate or_1, 9 bits wide
  Shifter #(.width(9), .shift("lr")) shifter_2 (.in(EAQ), .\dist (in_9), .out({out_18[8], A, out_18[3:0]}));
  assign out_11 = {{5{1'b0}}, multiplexer_1_out};  // Bit_Extender bit_extender_3
  Shifter #(.width(9), .shift("rr")) shifter_3 (.in(out_11), .\dist (in_3), .out(out_14));
  Register #(.width(9)) register_1 (.D({out_18[8], A, out_18[3:0]}), .clk(clock_2_out));  // open: en, Q, clr

  assign out_18[7:4] = A;
  assign Q = out_18[3:0];

  // Notes on the sheet:
  //   E
  //   E
  //   Q
  //   A
  //   Prajapati Krish S
  //   230280107116
endmodule
