// Logisim project prac 10 general register.circ as structural Verilog: 1 circuit, main circuit main
module main (
  input  [3:0] in_1,
  input  [2:0] in_2,
  input  [2:0] in_3,
  input  [3:0] OpCode,
  input  [3:0] in_5,
  input  [1:0] SHIFT_RIGHT_A,
  input  [2:0] in_7,
  input  [1:0] in_8
);

  wire clock_1_out, decoder_1_out0, decoder_1_out1, decoder_1_out2, decoder_1_out3, decoder_1_out4,
       decoder_1_out5, decoder_1_out6, decoder_1_out7;
  wire [3:0] A_B_out, adder_1_out, adder_2_out, adder_3_out, multiplexer_1_out, multiplexer_2_out,
       multiplexer_3_out, not_1_out, or_1_out, R0_q, R1_q, R2_q, R3_q, R4_q, R5_q, R6_q, R7_q, shifter_1_out,
       shifter_2_out, subtractor_1_out, xor_1_out;

  Decoder #(.select(3), .enable("false")) decoder_1 (
    .out0(decoder_1_out0), .out1(decoder_1_out1), .out2(decoder_1_out2), .out3(decoder_1_out3),
    .out4(decoder_1_out4), .out5(decoder_1_out5), .out6(decoder_1_out6), .out7(decoder_1_out7), .sel(in_7));
  Register #(.width(4)) R0 (.D(multiplexer_3_out), .en(decoder_1_out0), .Q(R0_q), .clk(clock_1_out));  // open: clr
  Register #(.width(4)) R1 (.D(multiplexer_3_out), .en(decoder_1_out1), .Q(R1_q), .clk(clock_1_out));  // open: clr
  Register #(.width(4)) R2 (.D(multiplexer_3_out), .en(decoder_1_out2), .Q(R2_q), .clk(clock_1_out));  // open: clr
  Register #(.width(4)) R3 (.D(multiplexer_3_out), .en(decoder_1_out3), .Q(R3_q), .clk(clock_1_out));  // open: clr
  Register #(.width(4)) R4 (.D(multiplexer_3_out), .en(decoder_1_out4), .Q(R4_q), .clk(clock_1_out));  // open: clr
  Register #(.width(4)) R5 (.D(multiplexer_3_out), .en(decoder_1_out5), .Q(R5_q), .clk(clock_1_out));  // open: clr
  Register #(.width(4)) R6 (.D(multiplexer_3_out), .en(decoder_1_out6), .Q(R6_q), .clk(clock_1_out));  // open: clr
  Register #(.width(4)) R7 (.D(multiplexer_3_out), .en(decoder_1_out7), .Q(R7_q), .clk(clock_1_out));  // open: clr
  Clock clock_1 (.out(clock_1_out));
  Multiplexer #(.select(3), .width(4), .enable("false")) multiplexer_1 (
    .in0(R0_q), .in1(R1_q), .in2(R2_q), .in3(R3_q), .in4(R4_q), .in5(R5_q), .in6(R6_q), .in7(R7_q),
    .out(multiplexer_1_out), .sel(in_2));
  Multiplexer #(.select(3), .width(4), .enable("false")) multiplexer_2 (
    .in0(R0_q), .in1(R1_q), .in2(R2_q), .in3(R3_q), .in4(R4_q), .in5(R5_q), .in6(R6_q), .in7(R7_q),
    .out(multiplexer_2_out), .sel(in_3));
  Shifter #(.width(4)) shifter_1 (.in(multiplexer_1_out), .\dist (in_8), .out(shifter_1_out));
  Adder #(.width(4)) adder_1 (.a(multiplexer_1_out), .b(in_1), .out(adder_1_out));  // open: cin, cout
  Adder #(.width(4)) adder_2 (.a(multiplexer_1_out), .b(multiplexer_2_out), .out(adder_2_out));  // open: cin, cout
  Subtractor #(.width(4)) subtractor_1 (
    .a(multiplexer_1_out), .b(multiplexer_2_out), .out(subtractor_1_out));  // open: bin, bout
  Adder #(.width(4)) adder_3 (.a(multiplexer_1_out), .b(in_5), .out(adder_3_out));  // open: cin, cout
  assign A_B_out = multiplexer_1_out & multiplexer_2_out;  // AND_Gate A_B, 4 bits wide
  assign or_1_out = multiplexer_1_out | multiplexer_2_out;  // OR_Gate or_1, 4 bits wide
  assign xor_1_out = multiplexer_1_out ^ multiplexer_2_out;  // XOR_Gate xor_1, 4 bits wide
  assign not_1_out = ~multiplexer_1_out;  // NOT_Gate not_1, 4 bits wide
  Shifter #(.width(4), .shift("lr")) shifter_2 (.in(multiplexer_1_out), .\dist (SHIFT_RIGHT_A), .out(shifter_2_out));
  Multiplexer #(.select(4), .width(4), .enable("false")) multiplexer_3 (
    .in0(multiplexer_1_out), .in1(adder_1_out), .in2(adder_2_out), .in3(subtractor_1_out), .in4(adder_3_out),
    .in5(A_B_out), .in6(or_1_out), .in7(xor_1_out), .in8(not_1_out), .in9(shifter_2_out),
    .in10(shifter_1_out), .out(multiplexer_3_out), .sel(OpCode));  // open: in11, in12, in13, in14, in15

  // Notes on the sheet:
  //   So we chose selection line of MUX A  accordingly
  //   The answer 7 in hexa is stored in R0 after giving clock.
  //   Practical 10 - General Register Organization
  //   B /B1
  //   here , R6 = f  , we want to right shift R6 , and store in R0 , so we choose opcode 1001 to perform the same.
  //   MUX A
  //   Prajapti Krish S
  //   230280107116
  //   MUX B
  //   B
  //   A
  //   ALU
  //   SHIFT LEFT A
  //   A+1
  //   A+B
  //   A-B
  //   A-1
  //   A OR B
  //   A XOR B
  //   NOT A
endmodule
