// Logisim project prac1register transfer.circ as structural Verilog: 1 circuit, main circuit main
// 2
module main (
  input  [3:0] in_1,
  input  [3:0] in_2,
  input  [3:0] in_3,
  input  [3:0] in_4,
  input  [1:0] in_5,
  input  in_6,
  input  [1:0] in_7,
  input  in_8,
  output [3:0] buffer
);

  wire clock_1_out, clock_2_out, decoder_1_out0, decoder_1_out1, decoder_1_out2, decoder_1_out3, not_1_out,
       not_2_out, not_3_out, not_4_out;
  wire [3:0] Register_A_q, Register_B_q, register_C_q, Register_D_2_q;

  Clock clock_1 (.out(clock_1_out));
  Register #(.width(4)) Register_A (.D(in_4), .Q(Register_A_q), .clk(clock_1_out));  // open: en, clr
  Multiplexer #(.select(2)) multiplexer_1 (
    .in0(Register_A_q[0]), .in1(Register_B_q[0]), .in2(register_C_q[0]), .in3(Register_D_2_q[0]),
    .out(buffer[0]), .sel(in_5), .en(in_6));
  Clock clock_2 (.out(clock_2_out));
  Register #(.width(4)) register_A_2 (.D(buffer), .clk(clock_2_out), .clr(not_1_out));  // open: en, Q
  not not_1 (not_1_out, decoder_1_out0);
  Register #(.width(4)) Register_B (.D(in_2), .Q(Register_B_q), .clk(clock_1_out));  // open: en, clr
  Multiplexer #(.select(2)) multiplexer_2 (
    .in0(Register_A_q[1]), .in1(Register_B_q[1]), .in2(register_C_q[1]), .in3(Register_D_2_q[1]),
    .out(buffer[1]), .sel(in_5), .en(in_6));
  Register #(.width(4)) register_B_2 (.D(buffer), .clk(clock_2_out), .clr(not_2_out));  // open: en, Q
  not not_2 (not_2_out, decoder_1_out1);
  Decoder #(.select(2)) decoder_1 (
    .out0(decoder_1_out0), .out1(decoder_1_out1), .out2(decoder_1_out2), .out3(decoder_1_out3), .sel(in_7),
    .en(in_8));
  Register #(.width(4)) register_C (.D(in_3), .Q(register_C_q), .clk(clock_1_out));  // open: en, clr
  Multiplexer #(.select(2)) multiplexer_3 (
    .in0(Register_A_q[2]), .in1(Register_B_q[2]), .in2(register_C_q[2]), .in3(Register_D_2_q[2]),
    .out(buffer[2]), .sel(in_5), .en(in_6));
  Register #(.width(4)) register_C_2 (.D(buffer), .clk(clock_2_out), .clr(not_3_out));  // open: en, Q
  not not_3 (not_3_out, decoder_1_out2);
  Register #(.width(4)) register_D (.D(buffer), .clk(clock_2_out), .clr(not_4_out));  // open: en, Q
  not not_4 (not_4_out, decoder_1_out3);
  Multiplexer #(.select(2)) multiplexer_4 (
    .in0(Register_A_q[3]), .in1(Register_B_q[3]), .in2(register_C_q[3]), .in3(Register_D_2_q[3]),
    .out(buffer[3]), .sel(in_5), .en(in_6));
  Register #(.width(4)) Register_D_2 (.D(in_1), .Q(Register_D_2_q), .clk(clock_1_out));  // open: en, clr

  // Notes on the sheet:
  //   Prac 1 : Register Transfer Operation
  //   A0
  //   D0
  //   bus line
  //   A1
  //   D1
  //   joining wires
  //   Prajapati Krish S
  //   230280107116
  //   Div -B / B1
  //   A2
  //   D2
  //   D3
  //   A3
endmodule
