// Logisim project prac3.circ as structural Verilog: 1 circuit, main circuit main
module main (
  input  A,
  input  B,
  input  [2:0] S2S1S0,
  output F
);

  wire and_1_out, buffer_1_out, nand_1_out, nor_1_out, not_1_out, or_1_out, xnor_1_out, xor_1_out;

  and and_1 (and_1_out, A, B);
  or or_1 (or_1_out, A, B);
  xor xor_1 (xor_1_out, A, B);
  not not_1 (not_1_out, A);
  nor nor_1 (nor_1_out, A, B);
  nand nand_1 (nand_1_out, A, B);
  xnor xnor_1 (xnor_1_out, A, B);
  buf buffer_1 (buffer_1_out, A);
  Multiplexer #(.select(3), .enable("false")) multiplexer_1 (
    .in0(and_1_out), .in1(or_1_out), .in2(xor_1_out), .in3(not_1_out), .in4(nor_1_out), .in5(nand_1_out),
    .in6(xnor_1_out), .in7(buffer_1_out), .out(F), .sel(S2S1S0));

  // Notes on the sheet:
  //   practical 3 : To Implement all logic operations in a singe circuit.
  //   Prajapati Krish S
  //   230280107116
  //   Div : B/B1
endmodule
