// Logisim project prac4common bus system.circ as structural Verilog: 1 circuit, main circuit main
module main (
  input  in_1,
  input  [2:0] in_2,
  input  in_3,
  input  in_4,
  input  [11:0] in_5,
  output [11:0] ADRESS,
  output [2:0] Opcode,
  output out_8
);

  wire clock_1_out, decoder_1_out0, demultiplexer_2_out1, demultiplexer_2_out2, demultiplexer_2_out3,
       demultiplexer_2_out5;
  wire [11:0] AR_q, multiplexer_1_out, PC_q;
  wire [15:0] AC_q, and_1_out, bit_extender_1_out, demultiplexer_1_out0, demultiplexer_1_out1, DR_q,
       ram_1_data;

  Clock clock_1 (.out(clock_1_out));
  Register #(.width(16)) IR (
    .D(demultiplexer_1_out0), .en(demultiplexer_2_out5), .Q({out_8, Opcode, ADRESS}), .clk(clock_1_out));  // open: clr
  Register #(.width(12)) AR (.D(PC_q), .en(demultiplexer_2_out1), .Q(AR_q), .clk(clock_1_out));  // open: clr
  Register #(.width(12)) PC (.D(in_5), .en(demultiplexer_2_out2), .Q(PC_q), .clk(clock_1_out));  // open: clr
  Multiplexer #(.width(12), .enable("false")) multiplexer_1 (
    .in0(AR_q), .in1(ADRESS), .out(multiplexer_1_out), .sel(in_4));
  RAM #(.addrWidth(12), .dataWidth(16)) ram_1 (
    .addr(multiplexer_1_out), .data(ram_1_data), .clk(clock_1_out));  // open: sel, ld, clr
  Demultiplexer #(.width(16), .enable("false")) demultiplexer_1 (
    .out0(demultiplexer_1_out0), .out1(demultiplexer_1_out1), .in(ram_1_data), .sel(in_3));
  Demultiplexer #(.select(3), .enable("false")) demultiplexer_2 (
    .out1(demultiplexer_2_out1), .out2(demultiplexer_2_out2), .out3(demultiplexer_2_out3),
    .out5(demultiplexer_2_out5), .in(in_1), .sel(in_2));  // open: out0, out4, out6, out7
  Decoder #(.select(3), .enable("false")) decoder_1 (
    .out0(decoder_1_out0), .sel(Opcode));  // open: out1, out2, out3, out4, out5, out6, out7
  Register #(.width(16)) DR (
    .D(demultiplexer_1_out1), .en(demultiplexer_2_out3), .Q(DR_q), .clk(clock_1_out));  // open: clr
  assign bit_extender_1_out = {{15{decoder_1_out0}}, decoder_1_out0};  // Bit_Extender bit_extender_1
  assign and_1_out = DR_q & AC_q & bit_extender_1_out;  // AND_Gate and_1, 16 bits wide
  Register #(.width(16)) AC (.D(and_1_out), .Q(AC_q), .clk(clock_1_out));  // open: en, clr

  // Notes on the sheet:
  //   Practical 4: Common Bus circuit
  //   8080 And 8008 = 8000
  //   Prajapati Krish S
  //   230280107116
  //   Div : B / B1
  //   AND
endmodule
