// Logisim project signed magnittude add sub prac 7.circ as structural Verilog: 1 circuit, main circuit main
module main (
  input  [3:0] A,
  input  [3:0] B,
  input  As,
  input  Bs,
  input  As_2,
  input  Bs_2,
  input  in_7,
  input  in_8,
  input  in_9,
  input  [3:0] in_10,
  input  [3:0] in_11,
  output out_12,
  output out_13,
  output sign_BIt,
  output [3:0] out_15,
  output Cout,
  output [3:0] out_17,
  output A_B,
  output sign_BIt_2,
  output sign_bit_3,
  output [3:0] out_21,
  output out_22,
  output sign_BIt_4,
  output A_B_2,
  output [3:0] out_25,
  output A_B_3,
  output [3:0] out_27
);

  wire adder_1_cout, and_1_out, comparator_1_eq, comparator_1_gt, comparator_1_lt, not_1_out, not_6_out,
       not_7_out, or_2_out;
  wire [3:0] adder_1_out, adder_3_out, controlled_buffer_2_out, not_3_out, not_5_out;

  // OR_Gate or_1 has open pins: in0=out_13, in1=in_8, out=open
  not not_1 (not_1_out, not_7_out);
  not not_2 (out_22, sign_bit_3);
  xor xor_1 (out_13, As_2, Bs_2);
  Adder #(.width(4)) adder_1 (.a(A), .b(not_3_out), .out(adder_1_out), .cin(in_9), .cout(adder_1_cout));
  assign out_17 = not_1_out ? adder_1_out : 4'bz;  // Controlled_Buffer controlled_buffer_1
  assign not_3_out = ~B;  // NOT_Gate not_3, 4 bits wide
  not not_4 (A_B, adder_1_cout);
  assign not_5_out = ~out_17;  // NOT_Gate not_5, 4 bits wide
  assign controlled_buffer_2_out = not_6_out ? not_5_out : 4'bz;  // Controlled_Buffer controlled_buffer_2
  not not_6 (not_6_out, adder_1_cout);
  Comparator #(.width(4)) comparator_1 (
    .a(out_17), .b(in_11), .gt(comparator_1_gt), .eq(comparator_1_eq), .lt(comparator_1_lt));
  or or_2 (or_2_out, comparator_1_gt, comparator_1_lt);
  assign A_B_3 = adder_1_cout ? comparator_1_eq : 1'bz;  // Controlled_Buffer controlled_buffer_3
  Adder #(.width(4)) adder_2 (.a(controlled_buffer_2_out), .b(in_10), .out(out_21));  // open: cin, cout
  assign A_B_2 = adder_1_cout ? or_2_out : 1'bz;  // Controlled_Buffer controlled_buffer_4
  xor xor_2 (out_12, As, Bs);
  and and_1 (and_1_out, out_12, in_7);
  Adder #(.width(4)) adder_3 (.a(B), .b(A), .out(adder_3_out), .cout(Cout));  // open: cin
  assign out_15 = not_7_out ? adder_3_out : 4'bz;  // Controlled_Buffer controlled_buffer_5
  not not_7 (not_7_out, and_1_out);

  assign out_25 = out_17;
  assign out_27 = out_17;
  assign sign_BIt = As;
  assign sign_BIt_2 = Bs;
  assign sign_BIt_4 = As;

  // Notes on the sheet:
  //   =0 Sutraction
  //   = 1 Additiion
  //   0 0 Subtraction
  //   1 1  Subtaction
  //   1 0 Addition
  //   01 Addititon
  //   Carry not generated
  //   Carry generated so ignore
  //   Additon operation
  //   =1 Sutraction
  //   =0 Addition
  //   230280107116
  //   Prajapati Krish S
  //   1 0 Subtraction
  //   01 SUbtraction
  //   0 0 Addition
  //   1 1 Addition
endmodule
